# Fritzing sketch bme_sensor (saved by Fritzing 0.9.4)

parts:
  Part1 = BME280 Breakout
  Raspberry_Pi_1 = Raspberry Pi 3 [part_number=RPI-3-V1.2]

nets:
  GND: Part1.GND, Raspberry_Pi_1.GND
  3.3V: Part1.3.3V, Raspberry_Pi_1.3v3
  N1: Part1.SDI/SDA, Raspberry_Pi_1.GPIO2
  N2: Part1.SCK/SCL, Raspberry_Pi_1.GPIO3
