# Fritzing sketch relay (saved by Fritzing 0.9.4)
breadboards: 1

parts:
  Raspberry_Pi_1 = Raspberry Pi 3 [part_number=RPI-3-V1.2]
  DS2Y-5-DC5V1 = DS2Y-5-DC5V [part_number=DS2Y-5-DC5V]
  Q1 = Basic FET N-Channel [package="DPak [SMD]"]
  J1 = Camdenboss CTB0158-2 [part_number=CTB0158-2 package=THT]
  D2 = Rectifier Diode [part_number=1N4001 package="300 mil [THT]"]

nets (from the schematic view):
  GND: Raspberry_Pi_1.GND, DS2Y-5-DC5V1.4_COM, Q1.source
  N1: Raspberry_Pi_1.GPIO23, Q1.Gate
  N2: Raspberry_Pi_1.5V, DS2Y-5-DC5V1.16_-, D2.cathode
  N3: DS2Y-5-DC5V1.8_N.O., J1.pin1
  N4: DS2Y-5-DC5V1.6_N.C., J1.pin2
  N5: DS2Y-5-DC5V1.1_+, Q1.drain, D2.anode
