# Fritzing sketch relay_light_sensor (saved by Fritzing 0.9.4)
breadboards: 1

parts:
  Raspberry_Pi_1 = Raspberry Pi 3 [part_number=RPI-3-V1.2]
  DS2Y-5-DC5V1 = DS2Y-5-DC5V [part_number=DS2Y-5-DC5V]
  Q1 = Basic FET N-Channel [package="DPak [SMD]"]
  D2 = Rectifier Diode [part_number=1N4001 package="300 mil [THT]"]
  LED1 = LED - 3mm [color="Green (560nm)" package="3 mm [THT]"]
  R1 = Resistor [tolerance=±5% resistance=220 package="0805 [SMD]"]
  DHT4 = DHT11 Humitidy and Temperature Sensor
  R4 = Resistor [tolerance=±5% resistance=10k package=THT]

nets (from the schematic view):
  N1: Raspberry_Pi_1.GPIO17, DHT4.DATA, R4.Pin_1
  GND: Raspberry_Pi_1.GND, DS2Y-5-DC5V1.4_COM, Q1.source, DHT4.GND
  N2: Raspberry_Pi_1.GPIO23, Q1.Gate
  5V: Raspberry_Pi_1.5V, DS2Y-5-DC5V1.16_-, D2.cathode, R1.Pin_0, DHT4.VDD, R4.Pin_0
  N3: DS2Y-5-DC5V1.8_N.O., LED1.cathode
  N4: DS2Y-5-DC5V1.1_+, Q1.drain, D2.anode
  N5: LED1.anode, R1.Pin_1

custom parts:
  DHT11 Humitidy and Temperature Sensor: DHT11 Humidity and Temperature Sensor
