# Fritzing sketch serial_node (saved by Fritzing 0.9.4)

parts:
  Raspberry_Pi_1 = Raspberry Pi 3 [part_number=RPI-3-V1.2]
  Part1 = Arduino Uno (Rev3)
  PART1 = SparkFun Soil Moisture Sensor [part_number=SEN-13322]

nets:
  GND: Raspberry_Pi_1.GND, Part1.GND, PART1.GND
  N1: Raspberry_Pi_1.GPIO15, Part1.D1/TX
  N2: Raspberry_Pi_1.GPIO14, Part1.D0/RX
  5V: Raspberry_Pi_1.5V, Part1.5V, PART1.VCC
  N3: Part1.A0, PART1.SIG

custom parts:
  SparkFun Soil Moisture Sensor: The SparkFun Soil Moisture Sensor is a simple breakout for measuring the moisture in soil and similar materials.
