# Fritzing sketch wifi_node (saved by Fritzing 0.9.4)

parts:
  PART1 = SparkFun Soil Moisture Sensor [part_number=SEN-13322]
  SparkFun_ESP32_Thing_Plus1 = SparkFun ESP32 Thing Plus [part_number=14689]

nets:
  VCC: PART1.VCC, SparkFun_ESP32_Thing_Plus1.3.3V
  GND: PART1.GND, SparkFun_ESP32_Thing_Plus1.GND
  N1: PART1.SIG, SparkFun_ESP32_Thing_Plus1.A0

custom parts:
  SparkFun Soil Moisture Sensor: The SparkFun Soil Moisture Sensor is a simple breakout for measuring the moisture in soil and similar materials.
  SparkFun ESP32 Thing Plus: The SparkFun ESP32 Thing Plus enjoys all the amenities of the ESP32 Thing, but with a few added sparkles. We've lengthened the board just a bit to accommodate a Qwiic connector for all your Qwiic breakout needs. We've also moved a few pins around to make the board compatible with the Adafruit Huzzah32 – ESP32 Feather Board such that you can use all of those lovely shields available out there!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
